// Digital circuit ProcesorProiectFIC.dig as structural Verilog
// The program counter.
// Here the current program counter is stored.
// The various inputs can be used to influence how the 
// program counter is modified if a clock signal happens.
// {{de Der Programmzähler. 
// Hier wird der aktuelle Programmzähler gespeichert. 
// Über die verschiedenen Eingänge kann beeinflußt 
// werden, auf welche Weise der Programmzähler mit 
// dem Takt weiter geschaltet wird.}}
module ProcesorProiectFIC (
  input  clock,
  input  [15:0] DataIN,
  input  storeInstrMem,
  input  resetPC,
  input  startSP
);

  wire ALU_p5, ALU_p6, ALU_p7, ALU_p9, ALU_p10, Carry, cmpImm1, cmpImm2, ControlUnit_writeregisterfile, enSP,
       InstructionDecoder_malu, InstructionDecoder_mload, InstructionDecoder_mmov, InstructionDecoder_mstore,
       jmpOp, loadOp, M, multiplexer_7_out, Neg, not_1_out, not_2_out, Overflow, reset_out, retOp, selPC,
       stackOp, strDM, usageALU, zero, ZeroFlag;
  wire [1:0] InstructionDecoder_mcmp, InstructionDecoder_rd, InstructionDecoder_rs1, InstructionDecoder_rs2;
  wire [4:0] InstructionDecoder_opcode;
  wire [10:0] InstructionDecoder_sgnext, InstructionDecoder_signext2;
  wire [15:0] ALU_p4, BranchingPC_s, DM_d, IM_d, multiplexer_1_out, multiplexer_2_out, multiplexer_3_out,
       multiplexer_4_out, multiplexer_5_out, multiplexer_6_out, multiplexer_8_out, multiplexer_9_out,
       multiplexer_10_out, multiplexer_11_out, multiplexer_12_out, multiplexer_13_out, multiplexer_14_out,
       multiplexer_15_out, multiplexer_16_out, multiplexer_17_out, one, PC_q, PCval, RegisterFile_rdest,
       RegisterFile_rsrc1, RegisterFile_rsrc2, SignExtend_immediate1, SignExtend_immediate2, SP_1_s,
       SP_plus_1_s, SP_q;

  Multiplexer #(.Bits(16)) multiplexer_1 (.sel(selPC), .in_0(PCval), .in_1(BranchingPC_s), .out(multiplexer_1_out));
  Multiplexer #(.Bits(16)) multiplexer_2 (
    .sel(resetPC), .in_0(multiplexer_1_out), .in_1({16{1'b0}}), .out(multiplexer_2_out));
  Register #(.Bits(16), .isProgramCounter("true")) PC (.D(multiplexer_2_out), .C(clock), .en(reset_out), .Q(PC_q));
  Reset reset (.out(reset_out));
  Add #(.Bits(16)) PC_plus_1 (.a(PC_q), .b(one), .c_i(zero), .s(PCval));  // open: c_o
  not not_1 (not_1_out, storeInstrMem);
  RAMDualPort #(.AddrBits(16), .isProgramMemory("true"), .Bits(16)) IM (
    .A(PC_q), .Din(DataIN), .str(storeInstrMem), .C(clock), .ld(not_1_out), .D(IM_d));
  InstructionDecoderProiectFIC InstructionDecoder (
    .Instruction(IM_d), .RD(InstructionDecoder_rd), .SgnExt(InstructionDecoder_sgnext),
    .RS2(InstructionDecoder_rs2), .RS1(InstructionDecoder_rs1), .SignExt2(InstructionDecoder_signext2),
    .MLoad(InstructionDecoder_mload), .MALU(InstructionDecoder_malu), .MStore(InstructionDecoder_mstore),
    .MMov(InstructionDecoder_mmov), .MCmp(InstructionDecoder_mcmp), .OpCode(InstructionDecoder_opcode));  // open: MPow, nopWE
  Add #(.Bits(16)) BranchingPC (.a({16{1'b0}}), .b(multiplexer_5_out), .c_i(zero), .s(BranchingPC_s));  // open: c_o
  ControlUnit ControlUnit (
    .OpCode(InstructionDecoder_opcode), .MCmp(InstructionDecoder_mcmp), .MLoad(InstructionDecoder_mload),
    .MStore(InstructionDecoder_mstore), .MALU(InstructionDecoder_malu), .MMov(InstructionDecoder_mmov),
    .ZERO_2(ZeroFlag), .NEG(Neg), .CARRY(Carry), .OVERFLOW(Overflow), .usageALU(usageALU), .M(M),
    .zero(zero), .one(one), .loadOp(loadOp), .cmpImmediate1(cmpImm1), .retOp(retOp), .jmpOp(jmpOp),
    .stackOp(stackOp), .selPC(selPC), .cmpImmediate2(cmpImm2),
    .writeRegisterFile(ControlUnit_writeregisterfile), .strDM(strDM));
  SignExtendUnit SignExtend (
    .SgnExt1(InstructionDecoder_sgnext), .SgnExt2(InstructionDecoder_signext2),
    .Immediate1(SignExtend_immediate1), .Immediate2(SignExtend_immediate2));
  Multiplexer #(.Bits(16)) multiplexer_3 (
    .sel(ALU_p10), .in_0(SignExtend_immediate1), .in_1(ALU_p4), .out(multiplexer_3_out));
  Multiplexer #(.Bits(16)) multiplexer_4 (.sel(loadOp), .in_0(multiplexer_3_out), .in_1(DM_d), .out(multiplexer_4_out));
  RegisterFileProiectFIC RegisterFile (
    .WD(multiplexer_4_out), .C(clock), .RS1(InstructionDecoder_rs1), .RD(InstructionDecoder_rd),
    .RS2(InstructionDecoder_rs2), .WE(ControlUnit_writeregisterfile), .Rdest(RegisterFile_rdest),
    .Rsrc1(RegisterFile_rsrc1), .Rsrc2(RegisterFile_rsrc2));
  Multiplexer #(.Bits(16)) multiplexer_5 (.sel(retOp), .in_0(ALU_p4), .in_1(DM_d), .out(multiplexer_5_out));
  Multiplexer #(.Bits(16)) multiplexer_6 (
    .sel(multiplexer_7_out), .in_0(RegisterFile_rsrc1), .in_1(RegisterFile_rsrc2), .out(multiplexer_6_out));
  Multiplexer multiplexer_7 (.sel(ALU_p10), .in_0(InstructionDecoder_rs2[0]), .in_1(ALU_p10), .out(multiplexer_7_out));
  Multiplexer #(.Bits(16)) multiplexer_8 (
    .sel(cmpImm1), .in_0(RegisterFile_rdest), .in_1(SignExtend_immediate1), .out(multiplexer_8_out));
  Multiplexer #(.Bits(16)) multiplexer_9 (
    .sel(M), .in_0(multiplexer_6_out), .in_1(SignExtend_immediate1), .out(multiplexer_9_out));
  Multiplexer #(.Bits(16)) multiplexer_10 (
    .sel(cmpImm2), .in_0(multiplexer_9_out), .in_1(SignExtend_immediate2), .out(multiplexer_10_out));
  // ALUProiectFIC ALU: pin names not known; wires that end beside it: multiplexer_8_out, multiplexer_10_out, InstructionDecoder_opcode, ALU_p4, ALU_p5, ALU_p6, ALU_p7, usageALU, ALU_p9, ALU_p10
  Multiplexer #(.Bits(16)) multiplexer_11 (
    .sel(jmpOp), .in_0(multiplexer_10_out), .in_1(PCval), .out(multiplexer_11_out));
  // FlagsRegisterFileProiectFic FlagsRegister: pin names not known; wires that end beside it: ALU_p5, clock, ALU_p6, ALU_p7, ALU_p9, ZeroFlag, Neg, Carry, Overflow
  Multiplexer #(.Bits(16)) multiplexer_12 (
    .sel(retOp), .in_0(multiplexer_11_out), .in_1({16{1'b0}}), .out(multiplexer_12_out));
  Multiplexer #(.Bits(16)) multiplexer_13 (
    .sel(stackOp), .in_0(ALU_p4), .in_1(multiplexer_16_out), .out(multiplexer_13_out));
  not not_2 (not_2_out, strDM);
  RAMDualPort #(.AddrBits(16), .isProgramMemory("true"), .Bits(16)) DM (
    .A(multiplexer_13_out), .Din(multiplexer_12_out), .str(strDM), .C(clock), .ld(not_2_out), .D(DM_d));
  Multiplexer #(.Bits(16)) multiplexer_14 (.sel(retOp), .in_0(SP_1_s), .in_1(SP_plus_1_s), .out(multiplexer_14_out));
  Multiplexer #(.Bits(16)) multiplexer_15 (
    .sel(stackOp), .in_0(SP_q), .in_1(multiplexer_14_out), .out(multiplexer_15_out));
  Multiplexer #(.Bits(16)) multiplexer_16 (
    .sel(retOp), .in_0(SP_q), .in_1(multiplexer_17_out), .out(multiplexer_16_out));
  Multiplexer #(.Bits(16)) multiplexer_17 (
    .sel(startSP), .in_0(multiplexer_15_out), .in_1({16{1'b1}}), .out(multiplexer_17_out));
  Sub #(.Bits(16)) SP_1 (.a(SP_q), .b(one), .c_i(zero), .s(SP_1_s));  // open: c_o
  Register #(.Bits(16)) SP (.D(multiplexer_17_out), .C(clock), .en(enSP), .Q(SP_q));
  Add #(.Bits(16)) SP_plus_1 (.a(SP_q), .b(one), .c_i(zero), .s(SP_plus_1_s));  // open: c_o
  or or_1 (enSP, stackOp, startSP);

  // Other names for the same wires on the sheet: clk = clock; rstPC = resetPC; strIM = storeInstrMem

  // Notes on the sheet:
  //   storeInstrMem: default 1
  //   startSP: default 1
endmodule
